# Fritzing sketch HistoRdualESP32inline (saved by Fritzing 0.9.3b)
stripboards: 2

parts:
  U1 = LuaNode32 / ESP32 [part_number=ESP32S-PIN30]
  U2 = LuaNode32 / ESP32 [part_number=ESP32S-PIN30]
  Součástka1 = MCU5102 I2S Stereo DAC  # not connected
  MCU5102_I2S_Stereo_DAC1_1 = MCU5102 I2S Stereo DAC  # not connected
  MCU5102_I2S_Stereo_DAC1_2 = MCU5102 I2S Stereo DAC  # not connected
  MCU5102_I2S_Stereo_DAC1_3 = MCU5102 I2S Stereo DAC  # not connected
  MCU5102_I2S_Stereo_DAC1_4 = MCU5102 I2S Stereo DAC  # not connected
  Součástka2 = LCD1602-I2C
  MCU5102_I2S_Stereo_DAC1 = MCU5102 I2S Stereo DAC
  Součástka6 = MCU5102 I2S Stereo DAC  # not connected
  MCU5102_I2S_Stereo_DAC1_1_2 = MCU5102 I2S Stereo DAC  # not connected
  MCU5102_I2S_Stereo_DAC1_2_2 = MCU5102 I2S Stereo DAC  # not connected
  MCU5102_I2S_Stereo_DAC1_3_2 = MCU5102 I2S Stereo DAC  # not connected
  MCU5102_I2S_Stereo_DAC1_4_2 = MCU5102 I2S Stereo DAC  # not connected
  XY-USB1 = XY-USB4
  microSD1 = MicroSD Card Module
  Součástka3 = Digital FM Radio Receiver
  Součástka4 = Si4713 Stereo FM Transmitter
  MCU5102_I2S_Stereo_DAC2 = MCU5102 I2S Stereo DAC
  Součástka7 = MCU5102 I2S Stereo DAC  # not connected
  MCU5102_I2S_Stereo_DAC2_1 = MCU5102 I2S Stereo DAC  # not connected
  MCU5102_I2S_Stereo_DAC2_2 = MCU5102 I2S Stereo DAC  # not connected
  MCU5102_I2S_Stereo_DAC2_3 = MCU5102 I2S Stereo DAC  # not connected
  MCU5102_I2S_Stereo_DAC2_4 = MCU5102 I2S Stereo DAC  # not connected
  5V = male pin header, 8 pins [form="♂ (male)"]
  3_3V_-_1 = male pin header, 8 pins [form="♂ (male)"]
  3_3V_-_2 = male pin header, 8 pins [form="♂ (male)"]
  SDA = male pin header, 3 pins [form="♂ (male)"]
  SCL = male pin header, 3 pins [form="♂ (male)"]
  Součástka5 = Adafruit Si5351A Clock Generator [part_number="Adafruit #2045"]
  KY-1 = Keyes Relay [package=THT]
  RelaySig = male pin header, 2 pins [form="♂ (male)"]
  5V_to_9V-12V_step-up = MT3608 Boost No usb
  5V_2 = male pin header, 5 pins [form="♂ (male)"]
  GND = male pin header, 5 pins [form="♂ (male)"]
  Součástka8 = TRRS 3.5mm Jack Breakout
  SCL_2 = male pin header, 3 pins [form="♂ (male)"]
  SDA_2 = male pin header, 3 pins [form="♂ (male)"]
  SDA1 = male pin header, 3 pins [form="♂ (male)"]
  SCL1 = male pin header, 3 pins [form="♂ (male)"]
  SCL2 = male pin header, 3 pins [form="♂ (male)"]
  SDA2 = male pin header, 3 pins [form="♂ (male)"]
  RelaySig1 = male pin header, 2 pins [form="♂ (male)"]
  GND1 = male pin header, 3 pins [form="♂ (male)"]
  5V1 = male pin header, 3 pins [form="♂ (male)"]
  MixerAudioIn = male pin header, 2 pins [form="♂ (male)"]
  MixerClkIn = male pin header, 2 pins [form="♂ (male)"]
  MixerRfOut = male pin header, 2 pins [form="♂ (male)"]
  AmplifierOut = male pin header, 2 pins [form="♂ (male)"]
  AmplifierIn = male pin header, 2 pins [form="♂ (male)"]
  Antena = male pin header, 1 pin [form="♂ (male)"]
  ANT1 = Antenna
  MixerPower = male pin header, 2 pins [form="♂ (male)"]
  AmplifierPower = male pin header, 2 pins [form="♂ (male)"]
  CD4066B1 = CD4066B
  CD4066B1_A = CD4066B  # not connected
  CD4066B1_B = CD4066B  # not connected
  CD4066B1_C = CD4066B  # not connected
  CD4066B1_D = CD4066B  # not connected
  CD4066B1_PWR = CD4066B  # not connected
  CD4066B2 = CD4066B
  CD4066B2_A = CD4066B  # not connected
  CD4066B2_B = CD4066B  # not connected
  CD4066B2_C = CD4066B  # not connected
  CD4066B2_D = CD4066B  # not connected
  CD4066B2_PWR = CD4066B  # not connected
  ESP1_DAC = TRRS 3.5mm Jack Breakout
  ESP2_DAC = TRRS 3.5mm Jack Breakout
  FMradio = TRRS 3.5mm Jack Breakout
  AMtransmitter = TRRS 3.5mm Jack Breakout
  FMtransmitter = TRRS 3.5mm Jack Breakout
  3_3V = male pin header, 2 pins [form="♂ (male)"]
  GND_2 = male pin header, 2 pins [form="♂ (male)"]
  C1 = male pin header, 2 pins [form="♂ (male)"]
  C2 = male pin header, 2 pins [form="♂ (male)"]
  C3 = male pin header, 2 pins [form="♂ (male)"]
  C4 = male pin header, 2 pins [form="♂ (male)"]
  C5 = male pin header, 2 pins [form="♂ (male)"]
  C1_2 = male pin header, 2 pins [form="♂ (male)"]
  C2_2 = male pin header, 2 pins [form="♂ (male)"]
  C3_2 = male pin header, 2 pins [form="♂ (male)"]
  C4_2 = male pin header, 2 pins [form="♂ (male)"]
  C5_2 = male pin header, 2 pins [form="♂ (male)"]
  3_3V_2 = male pin header, 3 pins [form="♂ (male)"]
  GND_3 = male pin header, 5 pins [form="♂ (male)"]
  J1 = male pin header, 5 pins [form="♂ (male)"]
  ON/OFF_switch = Toggle Switch [package=THT]
  DEBUG = Toggle Switch [package=THT]
  GND_4 = male pin header, 11 pins [form="♂ (male)"]
  ON/OFF_led = LED - 5mm [color="Red (633nm)" package="5 mm [THT]"]
  220-320_Ohm = Resistor [tolerance=±5% resistance=220 package=THT]

nets:
  N1: U1.EN, U1.D23, microSD1.MISO
  N2: U1.VP, U1.D22, SCL_2.pin2
  N3: U1.VN, U1.TX0
  N4: U1.D34, U1.RX0
  N5: U1.D35, U1.D21, SDA_2.pin2
  N6: U1.D32, U1.D19, microSD1.MOSI
  N7: U1.D33, U1.D18, microSD1.SCK
  N8: U1.D25, U1.D5, MCU5102_I2S_Stereo_DAC1.connector8, microSD1.CS
  N9: U1.D26, U1.TX2, MCU5102_I2S_Stereo_DAC1.connector6, MCU5102_I2S_Stereo_DAC1.connector13
  N10: U1.D27, U1.RX2, MCU5102_I2S_Stereo_DAC1.connector7
  N11: U1.D14, U1.D4
  N12: U1.D12, U1.D2
  N13: U1.D13, U1.D15
  N14: U1.GND, GND_4.pin7
  VIN: U1.Vin, U1.3V3, U2.Vin, U2.3V3, 3_3V_-_1.pin8, 3_3V_-_2.pin1, DEBUG.L2
  N15: U2.EN, U2.D23
  N16: U2.VP, U2.D22, SCL1.pin1
  N17: U2.VN, U2.TX0
  N18: U2.D34, U2.RX0
  N19: U2.D35, U2.D21, SDA1.pin1
  N20: U2.D32, U2.D19
  N21: U2.D33, U2.D18, Součástka3.!RST
  N22: U2.D25, U2.D5, Součástka4.CS, MCU5102_I2S_Stereo_DAC2.connector8, MCU5102_I2S_Stereo_DAC2.connector9
  N23: U2.D26, U2.TX2, MCU5102_I2S_Stereo_DAC2.connector6, MCU5102_I2S_Stereo_DAC2.connector13, SCL_2.pin3
  N24: U2.D27, U2.RX2, MCU5102_I2S_Stereo_DAC2.connector7, SDA_2.pin3
  N25: U2.D14, U2.D4
  N26: U2.D12, U2.D2
  N27: U2.D13, U2.D15
  N28: U2.GND, GND_4.pin6
  N29: Součástka2.GND, GND.pin4
  N30: Součástka2.VCC, 5V_2.pin4
  N31: Součástka2.SDA, SDA.pin2
  N32: Součástka2.SCL, SCL.pin2
  N33: MCU5102_I2S_Stereo_DAC1.connector0, 3_3V_-_1.pin7
  N34: MCU5102_I2S_Stereo_DAC1.connector2, GND_4.pin5
  N35: MCU5102_I2S_Stereo_DAC1.connector4, MCU5102_I2S_Stereo_DAC1.connector11
  N36: MCU5102_I2S_Stereo_DAC1.connector5, MCU5102_I2S_Stereo_DAC1.connector12
  N37: XY-USB1.connector4, GND_4.pin10
  N38: XY-USB1.connector7, ON/OFF_switch.L2
  N39: microSD1.GND, GND_4.pin4
  N40: microSD1.VCC, 5V.pin5
  N41: Součástka3.SCLK, SCL1.pin3
  N42: Součástka3.SDIO, SDA1.pin2
  N43: Součástka3.GND, GND_4.pin2
  N44: Součástka3.3.3V, 3_3V_-_2.pin2
  N45: Součástka4.VIN, 3_3V_-_2.pin3
  N46: Součástka4.GND, GND_4.pin1
  N47: Součástka4.SDA, SDA1.pin3
  N48: Součástka4.SCL, SCL1.pin2
  N49: MCU5102_I2S_Stereo_DAC2.connector0, MCU5102_I2S_Stereo_DAC2.connector1, 3_3V_-_2.pin4
  N50: MCU5102_I2S_Stereo_DAC2.connector2, MCU5102_I2S_Stereo_DAC2.connector3, GND_4.pin3
  N51: MCU5102_I2S_Stereo_DAC2.connector4, MCU5102_I2S_Stereo_DAC2.connector11
  N52: MCU5102_I2S_Stereo_DAC2.connector5, MCU5102_I2S_Stereo_DAC2.connector12
  N53: 5V.pin1, 220-320_Ohm.Pin_1
  N54: 5V.pin4, DEBUG.COM
  N55: 5V.pin6, 5V1.pin3
  N56: 5V.pin8, ON/OFF_switch.COM
  N57: 3_3V_-_1.pin6, 3_3V.pin1
  N58: SDA.pin1, Součástka5.SDA
  N59: SCL.pin1, Součástka5.SCL
  N60: Součástka5.VIN, 5V_2.pin1
  N61: Součástka5.GND, GND.pin1, MixerClkIn.pin1
  N62: Součástka5.CLK0, MixerClkIn.pin2
  N63: KY-1.signal, RelaySig.pin1
  N64: KY-1.power, GND.pin2
  N65: KY-1.ground, 5V_2.pin2
  N66: KY-1.NC, AmplifierOut.pin2, Antena.pin1, ANT1.antenna_lead
  N67: KY-1.C, MixerRfOut.pin1
  N68: KY-1.NO, AmplifierIn.pin2
  N69: 5V_to_9V-12V_step-up.IN_(-), 5V_to_9V-12V_step-up.OUT_(-), GND.pin3, MixerPower.pin2, AmplifierPower.pin2
  N70: 5V_to_9V-12V_step-up.IN_(+), 5V_2.pin3
  N71: 5V_to_9V-12V_step-up.OUT_(+), MixerPower.pin1, AmplifierPower.pin1
  N72: Součástka8.SLEEVE, MixerAudioIn.pin2
  N73: Součástka8.RING1, Součástka8.TIP, MixerAudioIn.pin1
  N74: SCL_2.pin1, SCL2.pin3
  N75: SDA_2.pin1, SDA2.pin3
  N76: RelaySig1.pin1, RelaySig1.pin2
  N77: GND1.pin3, GND_4.pin9
  N78: MixerRfOut.pin2, AmplifierIn.pin1
  N79: CD4066B1.connector0, ESP1_DAC.RING1, ESP1_DAC.TIP
  N80: CD4066B1.connector1, J1.pin2
  N81: CD4066B1.connector2, J1.pin1
  N82: CD4066B1.connector3, ESP2_DAC.RING1, ESP2_DAC.TIP
  N83: CD4066B1.connector4, C2_2.pin2
  N84: CD4066B1.connector5, C3_2.pin2
  N85: CD4066B1.connector6, GND_3.pin2
  N86: CD4066B1.connector7, FMradio.RING1, FMradio.TIP
  N87: CD4066B1.connector8, J1.pin3
  N88: CD4066B1.connector12, C1_2.pin2
  N89: CD4066B1.connector13, 3_3V_2.pin2
  N90: CD4066B2.connector0, J1.pin5
  N91: CD4066B2.connector1, AMtransmitter.RING1, AMtransmitter.TIP
  N92: CD4066B2.connector2, FMtransmitter.RING1, FMtransmitter.TIP
  N93: CD4066B2.connector3, J1.pin4
  N94: CD4066B2.connector4, C5_2.pin2
  N95: CD4066B2.connector6, GND_3.pin3
  N96: CD4066B2.connector12, C4_2.pin2
  N97: CD4066B2.connector13, 3_3V_2.pin3
  N98: ESP1_DAC.SLEEVE, ESP2_DAC.SLEEVE, FMradio.SLEEVE, GND_3.pin4
  N99: AMtransmitter.SLEEVE, FMtransmitter.SLEEVE, GND_3.pin5
  N100: GND_2.pin1, GND_4.pin8
  N101: C1.pin1, C1.pin2
  N102: C2.pin1, C2.pin2
  N103: C3.pin1, C3.pin2
  N104: C4.pin1, C4.pin2
  N105: C5.pin1, C5.pin2
  N106: GND_4.pin11, ON/OFF_led.cathode
  N107: ON/OFF_led.anode, 220-320_Ohm.Pin_0

notes:
  AM transmitter
  AudioSwitcher - 3 in - 2 out
  HistoR dual ESP32
  HistoR Display

custom parts:
  LuaNode32 / ESP32: New Image for LuaNode32 DOIT ESP32 DEVKIT V1. Base parts from LuaNode32 / ESP32 ESP32 based LuaNode32 by G.Noorlander DOIT Esp32 DevKit v1 (30 pins long, 11 pins width) by Werner Rothschopf (modified by vanepp Dec 2018)
  LCD1602-I2C: A standard character display, usually with 2x16 characters. Comes in many colors with LCM1602 IIC attached.
  XY-USB4: USB adapter with power and data lines output pins. USB A, USB C, Micro USB.
  Si4713 Stereo FM Transmitter: Yaaar! Become your very own pirate radio station with this FM radio transmitter. This breakout board, based on the best-of-class Si4713, is an all-in-one stereo audio FM transmitter that can also transmit RDS/RBDS data!
  Adafruit Si5351A Clock Generator: Never hunt around for another crystal again, with the Si5351A clock generator breakout from Adafruit! This chip has a precision 25MHz crystal reference and internal PLL and dividers so it can generate just about any frequency, from <8KHz up to 150+ MHz. The Si5351A clock generator is an I2C controller clock generator. It uses the onboard precision clock to drive multiple PLL's and clock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
  Keyes Relay: The Keyes 5V relay module is suitable for SCM development, home appliance control. It uses a 5V~12V TIL control signal which can control DC / AC signal.
  MT3608 Boost No usb: Chip- MT3608 / B6289 DC to DC step up, power booster module. With adjustable output voltage. Current- 2A . || Input voltage- 2V-24V || Output voltage- 5V-28V Input interface- Inversed polarity- NO. || Led indicator- No.
  CD4066B: CD4066B CMOS Quad Bilateral Switch
  CD4066B: CD4066B CMOS Quad Bilateral Switch
  CD4066B: CD4066B CMOS Quad Bilateral Switch
  CD4066B: CD4066B CMOS Quad Bilateral Switch
  CD4066B: CD4066B CMOS Quad Bilateral Switch
  CD4066B: CD4066B CMOS Quad Bilateral Switch
